# Fritzing sketch projet3-2 (saved by Fritzing 0.9.2b)
breadboards: 1

parts:
  Composant1 = Arduino Uno (Rev3) - ICSP
  Raspberry_Pi1 = Raspberry Pi B+
  S1 = H-Bridge with L298N
  M2 = DC Motor  # not connected
  S2 = Momentary Switch [package=ksa_sealed_tac_switch]
  S3 = Momentary Switch [package=ksa_sealed_tac_switch]

nets:
  N1: Composant1.A4/SDA, Raspberry_Pi1.GPIO2
  N2: Composant1.A5/SCL, Raspberry_Pi1.GPIO3
  N3: Composant1.D8, S1.IN2
  N4: Composant1.D9_PWM, S1.IN1
  5V: Composant1.5V, S1.5V, S2.2, S3.2
  GND: Composant1.GND, Raspberry_Pi1.GND, S1.GND

notes:
  Vers 12V batterie
  Blanc : vers ENA du L2698N
  I2C : Vert : SCL, Brun : SDA
  !!! En phase de développement, ce 5V de l'arduino est déconnecté car l'arduino est alimenté par USB !!!

custom parts:
  H-Bridge with L298N: h-bridge
