# Fritzing sketch projet3 (saved by Fritzing 0.9.2b)
breadboards: 1

parts:
  Composant1 = Arduino Uno (Rev3) - ICSP
  Raspberry_Pi1 = Raspberry Pi B+
  U2 = LCD-16X2 [package=lcd-16x2_noholes]  # not connected
  S1 = H-Bridge with L298N
  M2 = DC Motor  # not connected
  ACS712_Current_Sensor2 = ACS712 Current Sensor

nets:
  N1: Composant1.A1, ACS712_Current_Sensor2.OUT
  N2: Composant1.A4/SDA, Raspberry_Pi1.GPIO2
  N3: Composant1.A5/SCL, Raspberry_Pi1.GPIO3
  N4: Composant1.D2, S1.IN2
  N5: Composant1.D3_PWM, S1.IN1
  GND: Composant1.GND, Raspberry_Pi1.GND, S1.GND, ACS712_Current_Sensor2.GND

notes:
  Vers 12V batterie
  433MHz receiver
  Blanc : vers ENA du L2698N
  I2C : Vert : SCL, Brun : SDA

custom parts:
  H-Bridge with L298N: h-bridge
  ACS712 Current Sensor: A breakout board for the Allegro ACS712 is a Hall Effect-based linear current sensor. The module operates at 5V.
