# Fritzing sketch projet4 (saved by Fritzing 0.9.2b)
breadboards: 1

parts:
  Raspberry_Pi2 = Raspberry Pi 2
  Composant1 = Arduino Uno (Rev3) - ICSP
  M1 = DC Motor  # not connected
  S1 = H-Bridge with L298N
  ACS712_Current_Sensor1 = ACS712 Current Sensor  # not connected
  V1 = DC Power [voltage=5]  # not connected
  M2 = DC 5v-12V input to ± 12V DC-DC converter [package=THT]
  U2 = LCD-16X2 [package=lcd-8x2]  # not connected

nets:
  N1: Raspberry_Pi2.GPIO2, Composant1.A4/SDA
  N2: Raspberry_Pi2.GPIO3, Composant1.A5/SCL
  GND: Raspberry_Pi2.GND, Composant1.GND, S1.GND, M2.-12V
  N3: Raspberry_Pi2.GPIO20, S1.IN1
  N4: Raspberry_Pi2.GPIO16, S1.IN2
  5V: Composant1.5V, S1.5V, M2.+12V

notes:
  12V
  convertisseur 12V -> 5V
  +12V
  GND (- de la batterie 12V)
  Blanc : vers ENA du L2698N
  Vert : SCL, Brun : SDA

custom parts:
  H-Bridge with L298N: h-bridge
  ACS712 Current Sensor: A breakout board for the Allegro ACS712 is a Hall Effect-based linear current sensor. The module operates at 5V.
  DC 5v-12V input to ± 12V DC-DC converter: Input DC 5v-12v in to ± 12V DC- DC converter from ebay (search for ""Negative Voltage Dual DC12V""). Supplies ± 12V at up to 100MA output for op amps or rs232 drivers from a 5V to 12V input. Note the ground is not isolated (the two ground pins connect together internally). This module is larger and more expensive than the others, you might choose it despite that because it has dual regulators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
